# Fritzing sketch shield_afstandssensor (saved by Fritzing 1.0.4)

parts:
  Shield1 = Arduino Nano Shield V3
  Onderdeel1 = Arduino Nano RP2040 Connect  # not connected
  Sensor1 = RCWL-1601 ultrasone afstandssensor
  Stekker1 = Dagu DGServo 9g header connector (female) [package=THT]

nets:
  N1: Shield1.D7, Sensor1.TRIG
  VCC: Sensor1.VCC, Stekker1.Vcc
  N2: Sensor1.ECHO, Stekker1.pulse
  GND: Sensor1.GND, Stekker1.gnd

custom parts:
  Arduino Nano Shield V3: The Arduino Nano Shield is a compact and versatile accessory designed to simplify the development of Arduino Nano-based projects. This shield provides a convenient way to access all of the Nano's I/O pins, power connections, and additional features, making it ideal for prototyping and DIY electronics projects. Key Features: Pin Accessibility: Breaks out all 30 pins of the Arduino Nano to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
  RCWL-1601 ultrasone afstandssensor: Ultrasone afstandssensor RCWL-1601 (werkt op 3,3 V). Getekend op basis van het HC-SR04 uit fritzing-parts.
