# Fritzing sketch shield_ir_digitaal (saved by Fritzing 1.0.4)

parts:
  Shield1 = Arduino Nano Shield V3  # not connected
  Onderdeel1 = Arduino Nano RP2040 Connect  # not connected
  IR1 = ky-033 [package=THT]
  Stekker1 = Dagu DGServo 9g header connector (female) [package=THT]

nets:
  N1: IR1.pin2, Stekker1.pulse
  N2: IR1.pin3, Stekker1.gnd
  N3: IR1.pin4, Stekker1.Vcc

custom parts:
  Arduino Nano Shield V3: The Arduino Nano Shield is a compact and versatile accessory designed to simplify the development of Arduino Nano-based projects. This shield provides a convenient way to access all of the Nano's I/O pins, power connections, and additional features, making it ideal for prototyping and DIY electronics projects. Key Features: Pin Accessibility: Breaks out all 30 pins of the Arduino Nano to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
  ky-033: KY-033 Line successor module with TCRT5000 and analog output.
